// Logisim project ETFStudent.circ as structural Verilog: 2 circuits, main circuit KMADR
module KMADR (
  input  memdir,
  input  addr,
  input  immed,
  input  regind,
  input  regdir,
  input  brpom,
  input  bxpom,
  output [3:0] Adr3__0
);

  wire and_1_out, and_2_out, not_1_out, or_1_out, or_2_out;

  not not_1 (not_1_out, addr);
  assign Adr3__0 = not_1_out ? 4'b0000 : 4'bz;  // Controlled_Buffer controlled_buffer_1
  and and_1 (and_1_out, addr, or_1_out);
  assign Adr3__0 = and_1_out ? 4'b0001 : 4'bz;  // Controlled_Buffer controlled_buffer_2
  or or_1 (or_1_out, immed, regdir);
  and and_2 (and_2_out, addr, or_2_out);
  or or_2 (or_2_out, memdir, regind, brpom, bxpom);
  assign Adr3__0 = and_2_out ? 4'b0010 : 4'bz;  // Controlled_Buffer controlled_buffer_3
endmodule

module KMOPR (
  input  JMP,
  input  LD,
  input  AND,
  input  DEC,
  input  ADD,
  input  STBR,
  input  XOR,
  input  STAR,
  input  POP,
  input  RTS,
  input  STXR,
  input  STRLEN,
  input  HALT,
  input  JADR,
  input  EXEC,
  input  PUSH,
  input  JSR,
  input  RTI,
  input  JGRT,
  input  regdir,
  input  BNEQ,
  input  N,
  input  Z,
  input  BOVF,
  input  V,
  input  JNNG,
  input  ST,
  output [5:0] Adr5__0
);

  wire and_1_out, and_2_out, and_3_out, and_4_out, and_5_out, and_6_out, and_7_out, and_8_out, and_9_out,
       and_10_out, and_11_out, and_12_out, and_13_out, and_14_out, and_15_out, and_16_out, and_17_out,
       and_18_out, and_19_out, and_20_out, and_21_out, not_1_out, or_1_out, or_2_out, or_3_out, or_4_out,
       or_5_out, or_6_out, xor_1_out, xor_2_out;

  not not_1 (not_1_out, EXEC);
  assign Adr5__0 = not_1_out ? {6{1'b0}} : 6'bz;  // Controlled_Buffer controlled_buffer_1
  and and_1 (and_1_out, EXEC, STRLEN);
  assign Adr5__0 = and_1_out ? 6'b001111 : 6'bz;  // Controlled_Buffer controlled_buffer_2
  and and_2 (and_2_out, EXEC, HALT);
  assign Adr5__0 = and_2_out ? 6'b000001 : 6'bz;  // Controlled_Buffer controlled_buffer_3
  xor xor_1 (xor_1_out, N, V);
  or or_1 (or_1_out, xor_1_out, Z);
  and and_3 (and_3_out, or_1_out, JGRT);
  and and_4 (and_4_out, ~N, JNNG);  // AND_Gate
  and and_5 (and_5_out, ~Z, BNEQ);  // AND_Gate
  and and_6 (and_6_out, V, BOVF);
  or or_2 (or_2_out, JMP, and_3_out, and_4_out, and_5_out, and_6_out, JADR);
  and and_7 (and_7_out, EXEC, or_2_out);
  assign Adr5__0 = and_7_out ? 6'b001000 : 6'bz;  // Controlled_Buffer controlled_buffer_4
  xor xor_2 (xor_2_out, N, V);
  or or_3 (or_3_out, xor_2_out, Z);
  and and_8 (and_8_out, ~or_3_out, JGRT);  // AND_Gate
  and and_9 (and_9_out, Z, BNEQ);
  and and_10 (and_10_out, ~V, BOVF);  // AND_Gate
  and and_11 (and_11_out, N, JNNG);
  and and_12 (and_12_out, EXEC, or_4_out);
  or or_4 (or_4_out, and_8_out, and_9_out, and_10_out, and_11_out);
  assign Adr5__0 = and_12_out ? 6'b101111 : 6'bz;  // Controlled_Buffer controlled_buffer_5
  and and_13 (and_13_out, EXEC, or_5_out);
  assign Adr5__0 = and_13_out ? 6'b000011 : 6'bz;  // Controlled_Buffer controlled_buffer_6
  or or_5 (or_5_out, LD, AND, DEC, ADD, XOR);
  and and_14 (and_14_out, EXEC, ~regdir, ST);  // AND_Gate
  assign Adr5__0 = and_14_out ? 6'b101011 : 6'bz;  // Controlled_Buffer controlled_buffer_7
  and and_15 (and_15_out, ST, regdir);
  and and_16 (and_16_out, EXEC, or_6_out);
  assign Adr5__0 = and_16_out ? 6'b000010 : 6'bz;  // Controlled_Buffer controlled_buffer_8
  or or_6 (or_6_out, STBR, STAR, STXR, and_15_out);
  and and_17 (and_17_out, EXEC, POP);
  assign Adr5__0 = and_17_out ? 6'b001001 : 6'bz;  // Controlled_Buffer controlled_buffer_9
  and and_18 (and_18_out, EXEC, PUSH);
  assign Adr5__0 = and_18_out ? 6'b101000 : 6'bz;  // Controlled_Buffer controlled_buffer_10
  and and_19 (and_19_out, EXEC, JSR);
  and and_20 (and_20_out, EXEC, RTS);
  assign Adr5__0 = and_20_out ? {6{1'b1}} : 6'bz;  // Controlled_Buffer controlled_buffer_11
  assign Adr5__0 = and_19_out ? 6'b000100 : 6'bz;  // Controlled_Buffer controlled_buffer_12
  and and_21 (and_21_out, EXEC, RTI);
  assign Adr5__0 = and_21_out ? 6'b010100 : 6'bz;  // Controlled_Buffer controlled_buffer_13
endmodule
