// Logisim project ORT2Project.circ as structural Verilog: 8 circuits, main circuit COMPUTER
module COMPUTER (
);

  wire CLK, cpu_1_inta, interrupt_interface_8_1_p4, interrupt_interface_8_1_p5, interrupt_interface_8_1_p6,
       interrupt_interface_8_1_p7, interrupt_interface_8_1_p8, interrupt_interface_8_1_p9,
       interrupt_interface_8_1_p10, interrupt_interface_8_1_p11, pull_resistor_4_node, pull_resistor_5_node,
       ram_1_out_8, rst;
  wire [2:0] cpu_1_uext;
  wire [7:0] interrupt_interface_8_1_p1, pull_resistor_3_node, ram_1_dout;
  wire [15:0] pull_resistor_1_node;

  RAM ram_1 (
    .in_1(pull_resistor_1_node), .in_2(CLK), .in_3(pull_resistor_3_node), .in_4(pull_resistor_4_node),
    .in_5(pull_resistor_5_node), .in_6(rst), .DOUT(ram_1_dout), .out_8(ram_1_out_8));
  Pull_Resistor pull_resistor_1 (.node(pull_resistor_1_node));
  Pull_Resistor pull_resistor_2 (.node(ram_1_dout));
  Pull_Resistor pull_resistor_3 (.node(pull_resistor_3_node));
  Pull_Resistor pull_resistor_4 (.node(pull_resistor_4_node));
  Pull_Resistor pull_resistor_5 (.node(pull_resistor_5_node));
  Pull_Resistor pull_resistor_6 (.node(ram_1_out_8));
  CPU cpu_1 (
    .in_1(rst), .in_2(CLK), .in_3(ram_1_out_8), .in_4(ram_1_dout), .ABUS(pull_resistor_1_node),
    .DOUTBUS(pull_resistor_3_node), .out_8(pull_resistor_4_node), .out_9(pull_resistor_5_node),
    .inta(cpu_1_inta), .intr3__0(interrupt_interface_8_1_p1), .UEXT(cpu_1_uext));
  Button BTN_RST ();  // open: out
  Clock u_CLK (.out(CLK));
  // RisingEdge risingedge_1: pin names not known; wires that end beside it: 1'b1, 1'b1, CLK, rst
  // INTERRUPT_INTERFACE_8 interrupt_interface_8_1: pin names not known; wires that end beside it: interrupt_interface_8_1_p1, cpu_1_inta, cpu_1_uext, interrupt_interface_8_1_p4, interrupt_interface_8_1_p5, interrupt_interface_8_1_p6, interrupt_interface_8_1_p7, interrupt_interface_8_1_p8, interrupt_interface_8_1_p9, interrupt_interface_8_1_p10, interrupt_interface_8_1_p11, CLK
  Button BTN_INTR7 (.out(interrupt_interface_8_1_p4));
  Button BTN_INTR6 (.out(interrupt_interface_8_1_p5));
  Button BTN_INTR5 (.out(interrupt_interface_8_1_p6));
  Button BTN_INTR4 (.out(interrupt_interface_8_1_p7));
  Button BTN_INTR3 (.out(interrupt_interface_8_1_p8));
  Button BTN_INTR2 (.out(interrupt_interface_8_1_p9));
  Button BTN_INTR1 (.out(interrupt_interface_8_1_p10));
  Button BTN_INTR0 (.out(interrupt_interface_8_1_p11));
endmodule

module CPU (
  input  in_1,
  input  in_2,
  input  in_3,
  input  [7:0] in_4,
  input  [7:0] intr3__0,
  output [15:0] ABUS,
  output [7:0] DOUTBUS,
  output out_8,
  output out_9,
  output inta,
  output [2:0] UEXT
);

  wire [6:0] common_1_addrbus;
  wire [7:0] intr3__0_t;
  wire [8:0] pull_resistor_1_node;
  wire [15:0] A, B, INTRADDR, PSW;
  wire [22:0] pull_resistor_4_node;
  wire [26:0] common_1_coutbus;

  COMMON common_1 (
    .CLK(in_2), .RST(in_1), .DIN(in_4), .CinBUS(pull_resistor_4_node), .MAR(ABUS), .MDR(DOUTBUS),
    .CoutBUS(common_1_coutbus), .ADDRBUS(common_1_addrbus), .PSW_Output(PSW), .B(B), .A(A),
    .IVTPPDSP(INTRADDR), .PSW_Input(pull_resistor_1_node));
  Pull_Resistor pull_resistor_1 (.node(pull_resistor_1_node));
  Pull_Resistor pull_resistor_2 (.node(common_1_coutbus));
  Pull_Resistor pull_resistor_3 (.node(common_1_addrbus));
  Pull_Resistor pull_resistor_4 (.node(pull_resistor_4_node));
  FETCH fetch_1 (
    .in_1(in_1), .in_2(in_2), .in_3(in_3), .COMMONBUS(common_1_coutbus), .ADDRBUS(common_1_addrbus),
    .PSW(PSW), .rdMEM(out_9), .CMEMBUS(pull_resistor_4_node));
  ADDR addr_1 (
    .rdMEM(out_9), .CMEMBUS(pull_resistor_4_node), .in_1(in_1), .in_2(in_2), .in_3(in_3),
    .COMMONBUS(common_1_coutbus), .ADDRBUS(common_1_addrbus));
  EXEC exec_1 (
    .B(B), .PSW(PSW), .A(A), .CMEMBUS(pull_resistor_4_node), .rdMEM(out_8), .wrMEM(out_9), .in_1(in_1),
    .in_2(in_2), .in_3(in_3), .COMMONBUS(common_1_coutbus), .ADDRBUS(common_1_addrbus), .MDR(DOUTBUS),
    .CPSW(pull_resistor_1_node));
  INTR intr_1 (
    .PSW(PSW), .intr(intr3__0_t), .ADDIVTP(INTRADDR), .CMEMBUS(pull_resistor_4_node), .rdMEM(out_9),
    .wrMEM(out_8), .UEXT1__0(UEXT), .inta(inta), .in_1(in_1), .in_2(in_2), .in_3(in_3),
    .COMMONBUS(common_1_coutbus));

  // Other names for the same wires on the sheet: CLK = in_2; DIN7__0[7:0] = in_4; FCBUS = in_3; intr[7:0] = intr3__0;
  //   MAR[15:0] = ABUS; MDR[7:0] = DOUTBUS; RD = out_9; rst = in_1; WR = out_8
endmodule

module COMMON (
  input  CLK,
  input  RST,
  input  [7:0] DIN,
  input  [15:0] A,
  input  [15:0] IVTPPDSP,
  input  [22:0] CinBUS,
  input  [8:0] PSW_Input,
  output [15:0] MAR,
  output [7:0] MDR,
  output [15:0] B,
  output [26:0] CoutBUS,
  output [6:0] ADDRBUS,
  output [15:0] PSW_Output
);

  wire adrinst, and_3_out, and_4_out, and_5_out, and_7_out, and_8_out, and_9_out, and_10_out, and_11_out,
       and_12_out, and_13_out, and_14_out, and_15_out, and_16_out, and_17_out, and_18_out, and_19_out,
       and_20_out, and_21_out, and_22_out, and_23_out, and_24_out, and_25_out, and_26_out, bezadrinst,
       branchinst, counter_4_carry, decoder_1_out0, decoder_1_out1, decoder_1_out2, decoder_1_out5,
       decoder_1_out6, decoder_1_out7, decoder_1_out9, decoder_1_out10, decoder_1_out11, decoder_1_out13,
       decoder_1_out14, decoder_1_out15, decoder_3_out7, decoder_4_out5, decoder_4_out10, decoder_4_out11,
       decoder_4_out12, decoder_4_out13, decoder_4_out14, decoder_4_out15, decoder_5_out6, decoder_5_out7,
       grinst1, grinst2, grinst3, grinst4, grinst5, jmpinst, nor_1_out, or_2_out, or_3_out, or_5_out,
       or_6_out, or_7_out, or_8_out, or_11_out, or_12_out, or_13_out, or_14_out, or_15_out, or_16_out,
       or_17_out, or_18_out, or_19_out, or_20_out, or_21_out, or_22_out, or_23_out;
  wire [3:0] IR27__24;
  wire [7:0] inB7__0, inB15__8, inPC7__0, inPC15__8, IR7__0, multiplexer_1_out, multiplexer_2_out;
  wire [7:4] IR31__24;
  wire [15:0] AR, BR, brpomMEM, bxpomMEM, DR, inMAR, multiplexer_3_out, PC, PC_IR23__16, SP, XR;
  wire [15:8] IR15__0, IR23__8;

  Register register_1 (.D(MDR), .en(CinBUS[14]), .Q({IR31__24, IR27__24}), .clk(CLK));  // open: clr
  Decoder #(.select(4), .disabled(0)) decoder_1 (
    .out0(decoder_1_out0), .out1(decoder_1_out1), .out2(decoder_1_out2), .out3(adrinst), .out4(branchinst),
    .out5(decoder_1_out5), .out6(decoder_1_out6), .out7(decoder_1_out7), .out8(bezadrinst),
    .out9(decoder_1_out9), .out10(decoder_1_out10), .out11(decoder_1_out11), .out12(jmpinst),
    .out13(decoder_1_out13), .out14(decoder_1_out14), .out15(decoder_1_out15), .sel(IR31__24),
    .en(PSW_Output[0]));
  Decoder #(.select(2), .disabled(0)) decoder_2 (
    .out0(CoutBUS[13]), .out1(CoutBUS[14]), .out2(CoutBUS[15]), .out3(CoutBUS[16]), .sel(IR27__24[3:2]),
    .en(jmpinst));
  Decoder #(.select(3), .disabled(0)) decoder_3 (
    .out0(CoutBUS[19]), .out1(CoutBUS[20]), .out2(CoutBUS[21]), .out3(CoutBUS[22]), .out4(CoutBUS[23]),
    .out5(CoutBUS[24]), .out6(CoutBUS[25]), .out7(decoder_3_out7), .sel(IR27__24[3:1]), .en(adrinst));
  Counter #(.width(16), .max('hffff)) counter_1 (
    .load(CinBUS[4]), .D(inMAR), .count(CinBUS[5]), .Q(MAR), .clk(CLK));  // open: carry, clr
  or or_1 (grinst1, decoder_1_out15, decoder_1_out14, decoder_1_out13, decoder_1_out11, decoder_1_out10, decoder_1_out9, decoder_1_out7, decoder_1_out6, decoder_1_out5, decoder_1_out2, decoder_1_out1, decoder_1_out0);
  or or_2 (or_2_out, IR27__24[0], IR27__24[1]);
  and and_1 (grinst2, or_2_out, jmpinst);
  or or_3 (or_3_out, IR27__24[0], decoder_3_out7);
  and and_2 (grinst3, or_3_out, adrinst);
  Register register_2 (.D(MDR), .en(CinBUS[13]), .Q(IR23__8), .clk(CLK));  // open: clr
  Decoder #(.select(4), .disabled(0)) decoder_4 (
    .out0(CoutBUS[4]), .out1(CoutBUS[5]), .out2(CoutBUS[6]), .out3(CoutBUS[7]), .out4(CoutBUS[8]),
    .out5(decoder_4_out5), .out6(CoutBUS[9]), .out7(CoutBUS[10]), .out8(CoutBUS[11]), .out9(CoutBUS[12]),
    .out10(decoder_4_out10), .out11(decoder_4_out11), .out12(decoder_4_out12), .out13(decoder_4_out13),
    .out14(decoder_4_out14), .out15(decoder_4_out15), .sel(IR27__24), .en(bezadrinst));
  Multiplexer #(.select(3), .width(8), .disabled(0), .enable("false")) multiplexer_1 (
    .in0(DIN), .in1(PC[7:0]), .in2(PC[15:8]), .in3(A[7:0]), .in4(A[15:8]), .in5(PSW_Output[7:0]),
    .in6(PSW_Output[15:8]), .out(multiplexer_1_out), .sel(CinBUS[10:8]));  // open: in7
  Register register_3 (.D(MDR), .en(CinBUS[12]), .Q(IR15__0), .clk(CLK));  // open: clr
  or or_4 (grinst4, decoder_4_out15, decoder_4_out14, decoder_4_out13, decoder_4_out12, decoder_4_out11, decoder_4_out10, decoder_4_out5);
  Decoder #(.select(3), .disabled(0)) decoder_5 (
    .out0(ADDRBUS[0]), .out1(ADDRBUS[1]), .out2(ADDRBUS[2]), .out3(ADDRBUS[3]), .out4(ADDRBUS[4]),
    .out5(ADDRBUS[5]), .out6(decoder_5_out6), .out7(decoder_5_out7), .sel(IR23__8[15:13]), .en(adrinst));
  Register register_4 (.D(multiplexer_1_out), .en(CinBUS[7]), .Q(MDR), .clk(CLK));  // open: clr
  or or_5 (or_5_out, CoutBUS[24], CoutBUS[25]);
  or or_6 (or_6_out, IR23__8[8], IR23__8[9], IR23__8[10], IR23__8[11], IR23__8[12], decoder_5_out6, decoder_5_out7);
  and and_3 (and_3_out, or_6_out, adrinst);
  Register register_5 (.D(MDR), .en(CinBUS[11]), .Q(IR7__0), .clk(CLK));  // open: clr
  Decoder #(.disabled(0)) decoder_6 (.out0(CoutBUS[17]), .out1(CoutBUS[18]), .sel(IR27__24[3]), .en(branchinst));
  and and_4 (and_4_out, CoutBUS[20], ADDRBUS[0]);
  or or_7 (or_7_out, ADDRBUS[0], ADDRBUS[2]);
  and and_5 (and_5_out, or_7_out, or_5_out);
  or or_8 (or_8_out, IR27__24[0], IR27__24[1], IR27__24[2]);
  and and_6 (grinst5, or_8_out, branchinst);
  or or_9 (ADDRBUS[6], and_4_out, and_5_out, and_3_out);
  or or_10 (CoutBUS[26], grinst1, grinst2, grinst3, grinst4);
  S_R_Flip_Flop s_r_ff_1 (
    .S(CinBUS[0]), .clk(CLK), .R(or_11_out), .Q(CoutBUS[0]), .preset(RST));  // open: Qn, reset, en
  or or_11 (or_11_out, CinBUS[1], CinBUS[2]);
  S_R_Flip_Flop s_r_ff_2 (
    .S(CinBUS[1]), .clk(CLK), .R(CinBUS[2]), .Q(CoutBUS[1]), .reset(RST));  // open: Qn, preset, en
  or or_12 (or_12_out, RST, CinBUS[15]);
  or or_13 (or_13_out, CinBUS[15], CinBUS[16]);
  Register #(.width(16)) register_6 (.D(A), .en(and_7_out), .Q(DR), .clk(CLK));  // open: clr
  and and_7 (and_7_out, CinBUS[17], CoutBUS[20], ADDRBUS[2]);
  Register #(.width(16)) register_7 (.D(A), .en(and_8_out), .Q(AR), .clk(CLK));  // open: clr
  and and_8 (and_8_out, CinBUS[17], CoutBUS[12]);
  Register #(.width(16)) register_8 (.D(A), .en(and_9_out), .Q(BR), .clk(CLK));  // open: clr
  and and_9 (and_9_out, CinBUS[17], CoutBUS[10]);
  Register #(.width(16)) register_9 (.D(A), .en(and_10_out), .Q(XR), .clk(CLK));  // open: clr
  and and_10 (and_10_out, CinBUS[17], CoutBUS[11]);
  Adder #(.width(16)) adder_1 (.a(BR), .b({{8{1'b0}}, IR15__0}), .out(brpomMEM));  // open: cin, cout
  Register register_10 (.D(inB15__8), .en(CinBUS[19]), .Q(B[15:8]), .clk(CLK));  // open: clr
  or or_14 (or_14_out, CinBUS[21], RST);
  and and_11 (and_11_out, CinBUS[22], counter_4_carry);
  S_R_Flip_Flop s_r_ff_3 (
    .S(CinBUS[2]), .clk(CLK), .R(CinBUS[3]), .Q(CoutBUS[2]), .reset(RST));  // open: Qn, preset, en
  S_R_Flip_Flop s_r_ff_4 (
    .S(CinBUS[3]), .clk(CLK), .R(CinBUS[0]), .Q(CoutBUS[3]), .reset(RST));  // open: Qn, preset, en
  Counter #(.width(16), .max('hffff)) counter_2 (
    .load(or_12_out), .D(16'hf000), .count(or_13_out), .Q(SP), .clk(CLK));  // open: carry, clr
  Adder #(.width(16)) adder_2 (.a(brpomMEM), .b(XR), .out(bxpomMEM));  // open: cin, cout
  Register register_11 (.D(inB7__0), .en(CinBUS[18]), .Q(B[7:0]), .clk(CLK));  // open: clr
  Multiplexer #(.width(8), .disabled(0), .enable("false")) multiplexer_2 (
    .in0(inPC15__8), .in1(8'h10), .out(multiplexer_2_out), .sel(RST));
  Counter counter_3 (
    .load(or_14_out), .D(multiplexer_2_out), .count(and_11_out), .Q(PC[15:8]), .clk(CLK));  // open: carry, clr
  Adder #(.width(16)) adder_3 (.a(PC), .b({{8{1'b0}}, IR23__8}), .out(PC_IR23__16));  // open: cin, cout
  and and_12 (and_12_out, CoutBUS[1], ADDRBUS[5]);
  Counter counter_4 (
    .load(CinBUS[20]), .D(inPC7__0), .count(CinBUS[22]), .Q(PC[7:0]), .carry(counter_4_carry), .clk(CLK),
    .clr(RST));
  and and_13 (and_13_out, PSW_Input[1], CoutBUS[4]);
  and and_14 (and_14_out, PSW_Input[2], PSW_Input[8]);
  and and_15 (and_15_out, PSW_Input[2], PSW_Input[8]);
  assign PSW_Input[4] = CoutBUS[6] ? MDR[1] : 1'bz;  // Controlled_Buffer controlled_buffer_1
  assign PSW_Input[5] = CoutBUS[6] ? MDR[2] : 1'bz;  // Controlled_Buffer controlled_buffer_2
  assign PSW_Input[6] = CoutBUS[6] ? MDR[3] : 1'bz;  // Controlled_Buffer controlled_buffer_3
  assign PSW_Input[7] = CoutBUS[6] ? MDR[4] : 1'bz;  // Controlled_Buffer controlled_buffer_4
  assign inMAR = and_12_out ? bxpomMEM : 16'bz;  // Controlled_Buffer controlled_buffer_5
  Multiplexer #(.width(16), .enable("false")) multiplexer_3 (
    .in0(SP), .in1(IVTPPDSP), .out(multiplexer_3_out), .sel(CinBUS[6]));
  assign inB7__0 = nor_1_out ? MDR : 8'bz;  // Controlled_Buffer controlled_buffer_6
  nor nor_1 (nor_1_out, ADDRBUS[2], ADDRBUS[0]);
  assign inB15__8 = nor_1_out ? MDR : 8'bz;  // Controlled_Buffer controlled_buffer_7
  assign {inPC15__8, inPC7__0} = CoutBUS[25] ? MAR : 16'bz;  // Controlled_Buffer controlled_buffer_8
  S_R_Flip_Flop s_r_ff_5 (
    .S(PSW_Input[0]), .clk(CLK), .R(and_13_out), .Q(PSW_Output[0]), .preset(RST));  // open: Qn, reset, en
  S_R_Flip_Flop s_r_ff_6 (
    .S(and_14_out), .clk(CLK), .R(and_15_out), .Q(PSW_Output[15]), .preset(RST));  // open: Qn, reset, en
  assign PSW_Input[8] = CoutBUS[6] ? MDR[7] : 1'bz;  // Controlled_Buffer controlled_buffer_9
  and and_16 (and_16_out, CoutBUS[1], ADDRBUS[3]);
  assign inMAR = CoutBUS[3] ? multiplexer_3_out : 16'bz;  // Controlled_Buffer controlled_buffer_10
  assign inPC7__0 = or_15_out ? MDR : 8'bz;  // Controlled_Buffer controlled_buffer_11
  or or_15 (or_15_out, CoutBUS[5], CoutBUS[6]);
  assign inPC15__8 = or_15_out ? MDR : 8'bz;  // Controlled_Buffer controlled_buffer_12
  or or_16 (or_16_out, CoutBUS[7], CoutBUS[22]);
  or or_17 (or_17_out, CoutBUS[19], CoutBUS[21], CoutBUS[23]);
  assign inMAR = and_16_out ? AR : 16'bz;  // Controlled_Buffer controlled_buffer_13
  assign inMAR = and_17_out ? brpomMEM : 16'bz;  // Controlled_Buffer controlled_buffer_14
  and and_17 (and_17_out, CoutBUS[1], ADDRBUS[4]);
  assign inMAR = CoutBUS[0] ? PC : 16'bz;  // Controlled_Buffer controlled_buffer_15
  assign {inB15__8, inB7__0} = ADDRBUS[2] ? DR : 16'bz;  // Controlled_Buffer controlled_buffer_16
  assign {inB15__8, inB7__0} = ADDRBUS[0] ? {IR15__0, IR7__0} : 16'bz;  // Controlled_Buffer controlled_buffer_17
  assign {inPC15__8, inPC7__0} = or_18_out ? {IR23__8, IR15__0} : 16'bz;  // Controlled_Buffer controlled_buffer_18
  or or_18 (or_18_out, CoutBUS[15], CoutBUS[16], CoutBUS[18], CoutBUS[17]);
  or or_19 (or_19_out, CoutBUS[14], CoutBUS[13]);
  or or_20 (or_20_out, or_16_out, CoutBUS[24], CoutBUS[6]);
  or or_21 (or_21_out, or_16_out, CoutBUS[24], or_17_out, CoutBUS[6]);
  or or_22 (or_22_out, or_16_out, or_17_out, CoutBUS[6]);
  or or_23 (or_23_out, CoutBUS[6], or_16_out, CoutBUS[24]);
  assign inMAR = and_18_out ? {IR15__0, IR7__0} : 16'bz;  // Controlled_Buffer controlled_buffer_19
  and and_18 (and_18_out, CoutBUS[1], ADDRBUS[1]);
  assign inMAR = CoutBUS[2] ? SP : 16'bz;  // Controlled_Buffer controlled_buffer_20
  assign {inPC15__8, inPC7__0} = or_19_out ? PC_IR23__16 : 16'bz;  // Controlled_Buffer controlled_buffer_21
  and and_19 (and_19_out, PSW_Input[3], or_20_out, PSW_Input[4]);
  and and_20 (and_20_out, PSW_Input[3], or_20_out, ~PSW_Input[4]);  // AND_Gate
  and and_21 (and_21_out, PSW_Input[3], or_21_out, PSW_Input[6]);
  and and_22 (and_22_out, PSW_Input[3], or_21_out, ~PSW_Input[6]);  // AND_Gate
  and and_23 (and_23_out, PSW_Input[3], or_22_out, PSW_Input[7]);
  and and_24 (and_24_out, PSW_Input[3], or_22_out, ~PSW_Input[7]);  // AND_Gate
  and and_25 (and_25_out, PSW_Input[3], or_23_out, PSW_Input[5]);
  and and_26 (and_26_out, PSW_Input[3], or_23_out, ~PSW_Input[5]);  // AND_Gate
  S_R_Flip_Flop s_r_ff_7 (
    .S(and_19_out), .clk(CLK), .R(and_20_out), .Q(PSW_Output[1]), .reset(RST));  // open: Qn, preset, en
  S_R_Flip_Flop s_r_ff_8 (
    .S(and_21_out), .clk(CLK), .R(and_22_out), .Q(PSW_Output[3]), .reset(RST));  // open: Qn, preset, en
  S_R_Flip_Flop s_r_ff_9 (
    .S(and_23_out), .clk(CLK), .R(and_24_out), .Q(PSW_Output[4]), .reset(RST));  // open: Qn, preset, en
  S_R_Flip_Flop s_r_ff_10 (
    .S(and_25_out), .clk(CLK), .R(and_26_out), .Q(PSW_Output[2]), .reset(RST));  // open: Qn, preset, en

  // Other names for the same wires on the sheet: mxMDR0 = CinBUS[8]; mxMDR1 = CinBUS[9]; mxMDR2 = CinBUS[10];
  //   IR15__8[7:0] = IR15__0; IR23__8[7:0] = IR15__0; IR23__16[7:0] = IR23__8; A7__0[7:0] = A[7:0];
  //   A15__8[7:0] = A[15:8]; immed = ADDRBUS[0]; memdir = ADDRBUS[1]; regdir = ADDRBUS[2]; regind = ADDRBUS[3];
  //   brpom = ADDRBUS[4]; bxpom = ADDRBUS[5]; graddr = ADDRBUS[6]; stFETCH = CinBUS[0]; stADDR = CinBUS[1];
  //   stEXEC = CinBUS[2]; stINTR = CinBUS[3]; ldMAR = CinBUS[4]; incMAR = CinBUS[5]; mxMAR = CinBUS[6];
  //   ldMDR = CinBUS[7]; ldIR7__0 = CinBUS[11]; ldIR15__8 = CinBUS[12]; ldIR23__16 = CinBUS[13];
  //   ldIR31__24 = CinBUS[14]; decSP = CinBUS[15]; incSP = CinBUS[16]; ldReg = CinBUS[17]; ldB7__0 = CinBUS[18];
  //   ldB15__8 = CinBUS[19]; ldPC7__0 = CinBUS[20]; ldPC15__8 = CinBUS[21]; incPC = CinBUS[22]; FETCH = CoutBUS[0];
  //   ADDR = CoutBUS[1]; EXEC = CoutBUS[2]; INTR = CoutBUS[3]; HALT = CoutBUS[4]; RTS = CoutBUS[5]; RTI = CoutBUS[6];
  //   DEC = CoutBUS[7]; PUSH = CoutBUS[8]; POP = CoutBUS[9]; STBR = CoutBUS[10]; STXR = CoutBUS[11];
  //   STAR = CoutBUS[12]; BNEQ = CoutBUS[13]; BOVF = CoutBUS[14]; JNNG = CoutBUS[15]; JGRT = CoutBUS[16];
  //   JMP = CoutBUS[17]; JSR = CoutBUS[18]; LD = CoutBUS[19]; ST = CoutBUS[20]; AND = CoutBUS[21]; ADD = CoutBUS[22];
  //   XOR = CoutBUS[23]; STRLEN = CoutBUS[24]; JADR = CoutBUS[25]; grinst = CoutBUS[26]; DR7__0[7:0] = DR[7:0];
  //   DR15__8[7:0] = DR[15:8]; ENTRADDR15__0[15:0] = IVTPPDSP; IR15__0[7:0] = IR7__0; IR31__24[3:0] = IR27__24;
  //   PC7__0[7:0] = PC[7:0]; PC15__8[7:0] = PC[15:8]; stPSWS = PSW_Input[0]; clPSWS = PSW_Input[1];
  //   ldPSWI = PSW_Input[2]; ldPSW = PSW_Input[3]; V = PSW_Input[4]; C = PSW_Input[5]; Z = PSW_Input[6];
  //   N = PSW_Input[7]; I = PSW_Input[8]; PSW7__0[7:0] = PSW_Output[7:0]; PSWS = PSW_Output[0]; PSWV = PSW_Output[1];
  //   PSWC = PSW_Output[2]; PSWZ = PSW_Output[3]; PSWN = PSW_Output[4]; PSW15__8[7:0] = PSW_Output[15:8];
  //   PSWI = PSW_Output[15]

  // Notes on the sheet:
  //   Prepoznavanje instrukcije
  //   Instrukcijski registar
  //   MAR
  //   MDR
  //   Faze
  //   B
  //   SP
  //   PC
  //   Specijalizovani registri
  //   MAR Input
  //   Programska statusna reč (PSW)
endmodule

module FETCH (
  input  in_1,
  input  in_2,
  input  in_3,
  input  [26:0] COMMONBUS,
  input  [6:0] ADDRBUS,
  input  [15:0] PSW,
  output [22:0] CMEMBUS,
  output rdMEM
);

  wire addr2, addr3, addr_t, and_1_out, and_2_out, and_3_out, and_4_out, and_5_out, and_6_out, and_7_out,
       and_8_out, and_9_out, bezaddr1, braddr2, braddr3, brbezaddr1, brcnd, BRgraddr, BRgrinst, brjmp2,
       brjmp3, bruncnd, jmp2, jmp3, ldMAR, ldMDR, not_1_out, notFCBUS, notPSWSandFETCH, or_4_out, or_7_out,
       or_8_out, rdMEM_t, stEXEC;
  wire [7:0] counter_1_q, rom_1_data_2;
  wire [15:10] rom_1_data;

  or or_1 (bezaddr1, COMMONBUS[4], COMMONBUS[5], COMMONBUS[6], COMMONBUS[7], COMMONBUS[8], COMMONBUS[9], COMMONBUS[10], COMMONBUS[11], COMMONBUS[12]);
  or or_2 (jmp3, COMMONBUS[15], COMMONBUS[16], COMMONBUS[17], COMMONBUS[18]);
  or or_3 (jmp2, COMMONBUS[13], COMMONBUS[14]);
  Counter #(.trigger("falling")) counter_1 (
    .load(brcnd), .D(rom_1_data_2), .count(not_1_out), .Q(counter_1_q), .clk(in_2), .clr(in_1));  // open: carry
  not not_1 (not_1_out, brcnd);
  or or_4 (or_4_out, ~COMMONBUS[0], ~PSW[0]);  // OR_Gate
  and and_1 (and_1_out, bezaddr1, brbezaddr1);
  and and_2 (and_2_out, jmp2, brjmp2);
  and and_3 (and_3_out, addr2, braddr2);
  and and_4 (and_4_out, jmp3, brjmp3);
  and and_5 (and_5_out, addr3, braddr3);
  and and_6 (and_6_out, ~in_3, notFCBUS);  // AND_Gate
  and and_7 (and_7_out, COMMONBUS[26], BRgrinst);
  and and_8 (and_8_out, ADDRBUS[6], BRgraddr);
  or or_5 (addr_t, COMMONBUS[19], COMMONBUS[20], COMMONBUS[21], COMMONBUS[22], COMMONBUS[23], COMMONBUS[24], COMMONBUS[25]);
  and and_9 (and_9_out, or_4_out, notPSWSandFETCH);
  or or_6 (brcnd, and_9_out, and_1_out, and_2_out, and_3_out, and_4_out, and_5_out, and_6_out, and_7_out, and_8_out, bruncnd);
  or or_7 (or_7_out, ADDRBUS[2], ADDRBUS[3]);
  or or_8 (or_8_out, ADDRBUS[4], ADDRBUS[5]);
  ROM #(.dataWidth(24)) rom_1 (
    .addr(counter_1_q),
    .data({rom_1_data_2, rom_1_data, stEXEC, CMEMBUS[1], CMEMBUS[11], CMEMBUS[12], CMEMBUS[13], CMEMBUS[14], ldMDR, rdMEM_t, CMEMBUS[22], ldMAR}),
    .sel(1'b1));
  Decoder #(.select(4), .disabled(0), .enable("false")) decoder_1 (
    .out1(bruncnd), .out2(notPSWSandFETCH), .out3(BRgrinst), .out4(brbezaddr1), .out5(BRgraddr),
    .out6(brjmp2), .out7(braddr2), .out8(brjmp3), .out9(braddr3), .out15(notFCBUS), .sel(rom_1_data[15:12]));  // open: out0, out10, out11, out12, out13, out14
  and and_10 (addr2, or_7_out, addr_t);
  and and_11 (addr3, or_8_out, addr_t);
  assign CMEMBUS[4] = ldMAR ? 1'b1 : 1'bz;  // Controlled_Buffer controlled_buffer_1
  assign CMEMBUS[7] = ldMDR ? 1'b1 : 1'bz;  // Controlled_Buffer controlled_buffer_2
  assign CMEMBUS[2] = stEXEC ? 1'b1 : 1'bz;  // Controlled_Buffer controlled_buffer_3
  assign rdMEM = rdMEM_t ? 1'b1 : 1'bz;  // Controlled_Buffer controlled_buffer_4

  // Other names for the same wires on the sheet: immed = ADDRBUS[0]; memdir = ADDRBUS[1]; regdir = ADDRBUS[2];
  //   regind = ADDRBUS[3]; brpom = ADDRBUS[4]; bxpom = ADDRBUS[5]; graddr = ADDRBUS[6]; CLK = in_2;
  //   stADDR = CMEMBUS[1]; ldIR7__0 = CMEMBUS[11]; ldIR15__8 = CMEMBUS[12]; ldIR23__16 = CMEMBUS[13];
  //   ldIR31__24 = CMEMBUS[14]; incPC = CMEMBUS[22]; FETCH = COMMONBUS[0]; ADDR = COMMONBUS[1]; EXEC = COMMONBUS[2];
  //   INTR = COMMONBUS[3]; HALT = COMMONBUS[4]; RTS = COMMONBUS[5]; RTI = COMMONBUS[6]; DEC = COMMONBUS[7];
  //   PUSH = COMMONBUS[8]; POP = COMMONBUS[9]; STBR = COMMONBUS[10]; STXR = COMMONBUS[11]; STAR = COMMONBUS[12];
  //   BNEQ = COMMONBUS[13]; BOVF = COMMONBUS[14]; JNNG = COMMONBUS[15]; JGRT = COMMONBUS[16]; JMP = COMMONBUS[17];
  //   JSR = COMMONBUS[18]; LD = COMMONBUS[19]; ST = COMMONBUS[20]; AND = COMMONBUS[21]; ADD = COMMONBUS[22];
  //   XOR = COMMONBUS[23]; STRLEN = COMMONBUS[24]; JADR = COMMONBUS[25]; grinst = COMMONBUS[26]; FCBUS = in_3;
  //   PSWS = PSW[0]; PSWV = PSW[1]; PSWC = PSW[2]; PSWZ = PSW[3]; PSWN = PSW[4]; PSWI = PSW[15]; rst = in_1

  // Notes on the sheet:
  //   Operaciona jedinica
  //   Kontrolna jedinica
  //   contents of rom_1 (hex, n*v repeats v):
  //   2000 3 2f00c 3010 0 134000 3 7f00c 5020 136000 127000 3 cf00c 138040 129000 3 10f00c 80 2100 2200
endmodule

module ADDR (
  input  in_1,
  input  in_2,
  input  in_3,
  input  [26:0] COMMONBUS,
  input  [6:0] ADDRBUS,
  output [22:0] CMEMBUS,
  output rdMEM
);

  wire and_1_out, and_2_out, BRcnd, BRnotFCBUS, BRstANDjadr, BRunc, incMAR, ldMAR, ldMDR, mx, not_1_out,
       or_1_out, rdMEM_t, stEXEC;
  wire [3:0] counter_1_q, kmadr_1_adr3__0, multiplexer_1_out, rom_1_data_2;
  wire [11:8] rom_1_data;

  KMADR kmadr_1 (
    .Adr3__0(kmadr_1_adr3__0), .immed(ADDRBUS[0]), .addr(COMMONBUS[1]), .regdir(ADDRBUS[2]),
    .memdir(ADDRBUS[1]), .regind(ADDRBUS[3]), .brpom(ADDRBUS[4]), .bxpom(ADDRBUS[5]));
  Multiplexer #(.width(4), .enable("false")) multiplexer_1 (
    .in0(rom_1_data_2), .in1(kmadr_1_adr3__0), .out(multiplexer_1_out), .sel(mx));
  Counter #(.width(4), .max('hf)) counter_1 (
    .load(BRcnd), .D(multiplexer_1_out), .count(not_1_out), .Q(counter_1_q), .clk(in_2), .clr(in_1));  // open: carry
  not not_1 (not_1_out, BRcnd);
  and and_1 (and_1_out, BRnotFCBUS, ~in_3);  // AND_Gate
  and and_2 (and_2_out, BRstANDjadr, or_1_out);
  or or_1 (or_1_out, COMMONBUS[20], COMMONBUS[24], COMMONBUS[25]);
  or or_2 (BRcnd, and_1_out, and_2_out, BRunc, mx);
  ROM #(.addrWidth(4), .dataWidth(16)) rom_1 (
    .addr(counter_1_q),
    .data({rom_1_data_2, rom_1_data, stEXEC, incMAR, rdMEM_t, ldMDR, ldMAR, CMEMBUS[19:18], mx}), .sel(1'b1));
  Decoder #(.select(2), .enable("false")) decoder_1 (
    .out1(BRunc), .out2(BRstANDjadr), .out3(BRnotFCBUS), .sel(rom_1_data[9:8]));  // open: out0
  assign CMEMBUS[4] = ldMAR ? 1'b1 : 1'bz;  // Controlled_Buffer controlled_buffer_1
  assign CMEMBUS[7] = ldMDR ? 1'b1 : 1'bz;  // Controlled_Buffer controlled_buffer_2
  assign CMEMBUS[2] = stEXEC ? 1'b1 : 1'bz;  // Controlled_Buffer controlled_buffer_3
  assign CMEMBUS[5] = incMAR ? 1'b1 : 1'bz;  // Controlled_Buffer controlled_buffer_4
  assign rdMEM = rdMEM_t ? 1'b1 : 1'bz;  // Controlled_Buffer controlled_buffer_5

  // Other names for the same wires on the sheet: immed = ADDRBUS[0]; memdir = ADDRBUS[1]; regdir = ADDRBUS[2];
  //   regind = ADDRBUS[3]; brpom = ADDRBUS[4]; bxpom = ADDRBUS[5]; CLK = in_2; ldB7__0 = CMEMBUS[18];
  //   ldB15__8 = CMEMBUS[19]; ADDR = COMMONBUS[1]; ST = COMMONBUS[20]; STRLEN = COMMONBUS[24]; JADR = COMMONBUS[25];
  //   FCBUS = in_3; rst = in_1

  // Notes on the sheet:
  //   Upravljacka jedinica
  //   contents of rom_1 (hex, n*v repeats v):
  //   101 7106 7208 3330 44 5330 102 180
endmodule

module EXEC (
  input  in_1,
  input  in_2,
  input  in_3,
  input  [15:0] B,
  input  [7:0] MDR,
  input  [26:0] COMMONBUS,
  input  [6:0] ADDRBUS,
  input  [15:0] PSW,
  output [15:0] A,
  output [22:0] CMEMBUS,
  output [8:0] CPSW,
  output rdMEM,
  output wrMEM
);

  wire adder_1_cout, and_1_out, and_2_out, and_3_out, and_4_out, and_5_out, and_6_out, and_8_out, and_9_out,
       and_10_out, and_11_out, and_12_out, and_13_out, and_14_out, and_15_out, and_16_out, and_17_out, BRcnd,
       BRMDR_Z, BRnotFCBUS, BRunc, counter_1_carry, decSP, incA, incMAR, ldA7__0, ldA15__8, ldMAR, ldMDR,
       ldPC7__0, ldPC15__8, MDR_Z, mx, mxMDR0, mxMDR1, mxMDR2, not_1_out, or_1_out, or_4_out, rdMEM_t,
       subtractor_1_bout, wrMEM_t;
  wire [1:0] rom_1_data_2;
  wire [5:0] counter_3_q, kmopr_1_adr5__0, multiplexer_1_out;
  wire [6:0] Adata15__8;
  wire [7:0] Adata7__0;
  wire [15:0] adder_1_out, and_7_out, subtractor_1_out, xor_1_out;
  wire [29:21] rom_1_data;

  Counter counter_1 (
    .load(ldA7__0), .D(Adata7__0), .count(incA), .Q(A[7:0]), .carry(counter_1_carry), .clk(in_2), .clr(in_1));
  or or_1 (or_1_out, COMMONBUS[9], COMMONBUS[3], COMMONBUS[6]);
  nor nor_1 (MDR_Z, MDR[0], MDR[1], MDR[2], MDR[3], MDR[4], MDR[5], MDR[6], MDR[7]);
  assign Adata7__0 = or_1_out ? MDR : 8'bz;  // Controlled_Buffer controlled_buffer_1
  assign {CPSW[7], Adata15__8} = or_1_out ? MDR : 8'bz;  // Controlled_Buffer controlled_buffer_2
  and and_1 (and_1_out, counter_1_carry, incA);
  Counter counter_2 (
    .load(ldA15__8), .D({CPSW[7], Adata15__8}), .count(and_1_out), .Q(A[15:8]), .clk(in_2), .clr(in_1));  // open: carry
  and and_2 (and_2_out, COMMONBUS[7], subtractor_1_bout);
  or or_2 (CPSW[5], and_2_out, and_3_out);
  and and_3 (and_3_out, COMMONBUS[22], adder_1_cout);
  and and_4 (and_4_out, COMMONBUS[22], ~COMMONBUS[3]);  // AND_Gate
  KMOPR kmopr_1 (
    .RTS(COMMONBUS[5]), .RTI(COMMONBUS[6]), .DEC(COMMONBUS[7]), .POP(COMMONBUS[9]), .STBR(COMMONBUS[10]),
    .Adr5__0(kmopr_1_adr5__0), .PUSH(COMMONBUS[8]), .regdir(ADDRBUS[2]), .JSR(COMMONBUS[18]),
    .LD(COMMONBUS[19]), .AND(COMMONBUS[21]), .ADD(COMMONBUS[22]), .XOR(COMMONBUS[23]),
    .STRLEN(COMMONBUS[24]), .EXEC(COMMONBUS[2]), .N(PSW[4]), .Z(PSW[3]), .V(PSW[1]), .JGRT(COMMONBUS[16]),
    .BNEQ(COMMONBUS[13]), .BOVF(COMMONBUS[14]), .JNNG(COMMONBUS[15]), .JADR(COMMONBUS[25]),
    .HALT(COMMONBUS[4]), .STAR(COMMONBUS[12]), .STXR(COMMONBUS[11]), .ST(COMMONBUS[20]), .JMP(COMMONBUS[17]));
  Multiplexer #(.width(6), .enable("false")) multiplexer_1 (
    .in0(rom_1_data[29:24]), .in1(kmopr_1_adr5__0), .out(multiplexer_1_out), .sel(mx));
  not not_1 (not_1_out, BRcnd);
  and and_5 (and_5_out, ~in_3, BRnotFCBUS);  // AND_Gate
  and and_6 (and_6_out, MDR_Z, BRMDR_Z);
  assign and_7_out = A & B;  // AND_Gate and_7, 16 bits wide
  assign xor_1_out = A ^ B;  // XOR_Gate xor_1, 16 bits wide
  Subtractor #(.width(16)) subtractor_1 (
    .a(A), .b(16'h1), .out(subtractor_1_out), .bout(subtractor_1_bout));  // open: bin
  Counter #(.width(6), .max('h3f)) counter_3 (
    .load(BRcnd), .D(multiplexer_1_out), .count(not_1_out), .Q(counter_3_q), .clk(in_2), .clr(in_1));  // open: carry
  or or_3 (BRcnd, BRunc, and_5_out, and_6_out, mx);
  assign {CPSW[7], Adata15__8, Adata7__0} = and_8_out ? and_7_out : 16'bz;  // Controlled_Buffer controlled_buffer_3
  and and_8 (and_8_out, COMMONBUS[21], ~COMMONBUS[3]);  // AND_Gate
  Pull_Resistor pull_resistor_1 (.node({CPSW[7], Adata15__8, Adata7__0}));
  assign {CPSW[7], Adata15__8, Adata7__0} = and_9_out ? B : 16'bz;  // Controlled_Buffer controlled_buffer_4
  and and_9 (and_9_out, COMMONBUS[19], ~COMMONBUS[3]);  // AND_Gate
  assign {CPSW[7], Adata15__8, Adata7__0} = and_10_out ? xor_1_out : 16'bz;  // Controlled_Buffer controlled_buffer_5
  and and_10 (and_10_out, COMMONBUS[23], ~COMMONBUS[3]);  // AND_Gate
  assign {CPSW[7], Adata15__8, Adata7__0} = and_11_out ? subtractor_1_out : 16'bz;  // Controlled_Buffer controlled_buffer_6
  and and_11 (and_11_out, COMMONBUS[7], ~COMMONBUS[3]);  // AND_Gate
  assign {CPSW[7], Adata15__8, Adata7__0} = and_12_out ? {16{1'b0}} : 16'bz;  // Controlled_Buffer controlled_buffer_7
  and and_12 (and_12_out, COMMONBUS[24], ~COMMONBUS[3]);  // AND_Gate
  Adder #(.width(16)) adder_1 (.a(A), .b(B), .out(adder_1_out), .cout(adder_1_cout));  // open: cin
  assign {CPSW[7], Adata15__8, Adata7__0} = and_4_out ? adder_1_out : 16'bz;  // Controlled_Buffer controlled_buffer_8
  Decoder #(.select(2), .enable("false")) decoder_1 (
    .out1(BRunc), .out2(BRMDR_Z), .out3(BRnotFCBUS), .sel(rom_1_data_2));  // open: out0
  nor nor_2 (CPSW[6], Adata7__0[0], Adata7__0[1], Adata7__0[2], Adata7__0[3], Adata7__0[4], Adata7__0[5], Adata7__0[6], Adata7__0[7], Adata15__8[1], Adata15__8[2], Adata15__8[3], Adata15__8[4], Adata15__8[5], Adata15__8[6], CPSW[7], Adata15__8[0]);
  ROM #(.addrWidth(6), .dataWidth(30)) rom_1 (
    .addr(counter_3_q),
    .data({rom_1_data[29:24], rom_1_data_2, rom_1_data[21], CMEMBUS[3], CPSW[2:1], CPSW[3], CMEMBUS[17], ldPC15__8, ldPC7__0, decSP, CMEMBUS[16], mxMDR2, mxMDR1, mxMDR0, ldMDR, incMAR, ldMAR, wrMEM_t, rdMEM_t, incA, ldA15__8, ldA7__0, mx}),
    .sel(1'b1));
  and and_13 (and_13_out, ~A[15], COMMONBUS[7], CPSW[7]);  // AND_Gate
  and and_14 (and_14_out, CPSW[7], COMMONBUS[24]);
  and and_15 (and_15_out, ~CPSW[7], B[15], A[15]);  // AND_Gate
  or or_4 (or_4_out, and_15_out, and_16_out);
  and and_16 (and_16_out, CPSW[7], ~B[15], ~A[15]);  // AND_Gate
  and and_17 (and_17_out, COMMONBUS[22], or_4_out);
  or or_5 (CPSW[4], and_13_out, and_14_out, and_17_out);
  assign CMEMBUS[7] = ldMDR ? 1'b1 : 1'bz;  // Controlled_Buffer controlled_buffer_9
  assign CMEMBUS[8] = mxMDR0 ? 1'b1 : 1'bz;  // Controlled_Buffer controlled_buffer_10
  assign CMEMBUS[9] = mxMDR1 ? 1'b1 : 1'bz;  // Controlled_Buffer controlled_buffer_11
  assign CMEMBUS[10] = mxMDR2 ? 1'b1 : 1'bz;  // Controlled_Buffer controlled_buffer_12
  assign CMEMBUS[15] = decSP ? 1'b1 : 1'bz;  // Controlled_Buffer controlled_buffer_13
  assign CMEMBUS[4] = ldMAR ? 1'b1 : 1'bz;  // Controlled_Buffer controlled_buffer_14
  assign CMEMBUS[5] = incMAR ? 1'b1 : 1'bz;  // Controlled_Buffer controlled_buffer_15
  assign CMEMBUS[20] = ldPC7__0 ? 1'b1 : 1'bz;  // Controlled_Buffer controlled_buffer_16
  assign CMEMBUS[21] = ldPC15__8 ? 1'b1 : 1'bz;  // Controlled_Buffer controlled_buffer_17
  assign rdMEM = rdMEM_t ? 1'b1 : 1'bz;  // Controlled_Buffer controlled_buffer_18
  assign wrMEM = wrMEM_t ? 1'b1 : 1'bz;  // Controlled_Buffer controlled_buffer_19

  // Other names for the same wires on the sheet: A7__0[7:0] = A[7:0]; A15__8[7:0] = A[15:8]; regdir = ADDRBUS[2];
  //   CLK = in_2; stINTR = CMEMBUS[3]; incSP = CMEMBUS[16]; ldReg = CMEMBUS[17]; EXEC = COMMONBUS[2];
  //   INTR = COMMONBUS[3]; HALT = COMMONBUS[4]; RTS = COMMONBUS[5]; RTI = COMMONBUS[6]; DEC = COMMONBUS[7];
  //   PUSH = COMMONBUS[8]; POP = COMMONBUS[9]; STBR = COMMONBUS[10]; STXR = COMMONBUS[11]; STAR = COMMONBUS[12];
  //   BNEQ = COMMONBUS[13]; BOVF = COMMONBUS[14]; JNNG = COMMONBUS[15]; JGRT = COMMONBUS[16]; JMP = COMMONBUS[17];
  //   JSR = COMMONBUS[18]; LD = COMMONBUS[19]; ST = COMMONBUS[20]; AND = COMMONBUS[21]; ADD = COMMONBUS[22];
  //   XOR = COMMONBUS[23]; STRLEN = COMMONBUS[24]; JADR = COMMONBUS[25]; grinst = COMMONBUS[26]; clPSWS = CPSW[1];
  //   ldPSWI = CPSW[2]; ldPSW = CPSW[3]; V = CPSW[4]; C = CPSW[5]; Z = CPSW[6]; Adata15__8[7] = CPSW[7]; N = CPSW[7];
  //   FCBUS = in_3; PSWS = PSW[0]; PSWV = PSW[1]; PSWC = PSW[2]; PSWZ = PSW[3]; PSWN = PSW[4]; PSWI = PSW[15];
  //   rst = in_1

  // Notes on the sheet:
  //   Operaciona jedinica
  //   Upravljacka jedinica
  //   contents of rom_1 (hex, n*v repeats v):
  //   1 2f440000 2f410000 2f420006 2540 5c00020 2340 7c00020 2f40c000 1000 1040 bc00110 44 dc00110
  //   2f400002 2 10c00110 13800000 10400088 2f420000 1000 40 16c00110 81000 40 19c00110 21000 40 1cc00110
  //   1004 40 1fc00110 2 1000 40 23c00110 9000 40 110 2f404000 2740 29c00020 2e402540 700 2cc00020 580
  //   2ec00020 500000
endmodule

module INTR (
  input  in_1,
  input  in_2,
  input  in_3,
  input  [7:0] intr,
  input  [26:0] COMMONBUS,
  input  [15:0] PSW,
  output inta,
  output [15:0] ADDIVTP,
  output [2:0] UEXT1__0,
  output rdMEM,
  output wrMEM,
  output [22:0] CMEMBUS
);

  wire and_1_out, and_2_out, and_3_out, and_4_out, brcnd, brnot_FCBUS, brnot_INTR, brnot_prekid, bruncnd,
       decSP, incMAR, ldMAR, ldMDR, ldPC7__0, ldPC15__8, mxMDR0, mxMDR1, mxMDR2, not_1_out, prper, rdMEM_t,
       wrMEM_t;
  wire [2:0] register_1_q, rom_1_data_2;
  wire [4:0] counter_1_q, rom_1_data_3;
  wire [15:0] addIVTP_t, IVTP;
  wire [19:14] rom_1_data;

  Priority_Encoder priority_encoder_1 (
    .in0(intr[0]), .in1(intr[1]), .in2(intr[2]), .in3(intr[3]), .in4(intr[4]), .in5(intr[5]), .in6(intr[6]),
    .in7(intr[7]), .out(UEXT1__0), .gs(prper));  // open: en_in, en_out
  Counter #(.width(5), .max('h1f), .trigger("falling")) counter_1 (
    .load(brcnd), .D(rom_1_data_3), .count(not_1_out), .Q(counter_1_q), .clk(in_2), .clr(in_1));  // open: carry
  not not_1 (not_1_out, brcnd);
  and and_1 (and_1_out, ~COMMONBUS[4], PSW[15], prper);  // AND_Gate
  and and_2 (and_2_out, ~in_3, brnot_FCBUS);  // AND_Gate
  Register #(.width(3)) register_1 (.D(UEXT1__0), .en(inta), .Q(register_1_q), .clk(in_2));  // open: clr
  and and_3 (and_3_out, ~COMMONBUS[3], brnot_INTR);  // AND_Gate
  and and_4 (and_4_out, ~and_1_out, brnot_prekid);  // AND_Gate
  or or_1 (brcnd, and_3_out, and_4_out, and_2_out, bruncnd);
  Register #(.width(16)) register_2 (.Q(IVTP), .clk(in_2), .clr(in_1));  // open: D, en
  ROM #(.addrWidth(5), .dataWidth(25)) rom_1 (
    .addr(counter_1_q),
    .data({rom_1_data_3, rom_1_data[19], rom_1_data_2, rom_1_data[15:14], CMEMBUS[0], incMAR, inta, ldPC7__0, ldPC15__8, mxMDR2, mxMDR1, mxMDR0, CMEMBUS[6], wrMEM_t, rdMEM_t, ldMDR, ldMAR, decSP}),
    .sel(1'b1));
  Decoder #(.select(3), .disabled(0), .enable("false")) decoder_1 (
    .out1(bruncnd), .out2(brnot_INTR), .out3(brnot_prekid), .out7(brnot_FCBUS), .sel(rom_1_data_2));  // open: out0, out4, out5, out6
  Adder #(.width(16)) adder_1 (.a(IVTP), .b({{12{1'b0}}, register_1_q, 1'b0}), .out(addIVTP_t));  // open: cin, cout
  assign rdMEM = rdMEM_t ? 1'b1 : 1'bz;  // Controlled_Buffer controlled_buffer_1
  assign wrMEM = wrMEM_t ? 1'b1 : 1'bz;  // Controlled_Buffer controlled_buffer_2
  assign CMEMBUS[4] = ldMAR ? 1'b1 : 1'bz;  // Controlled_Buffer controlled_buffer_3
  assign CMEMBUS[5] = incMAR ? 1'b1 : 1'bz;  // Controlled_Buffer controlled_buffer_4
  assign CMEMBUS[7] = ldMDR ? 1'b1 : 1'bz;  // Controlled_Buffer controlled_buffer_5
  assign CMEMBUS[8] = mxMDR0 ? 1'b1 : 1'bz;  // Controlled_Buffer controlled_buffer_6
  assign CMEMBUS[9] = mxMDR1 ? 1'b1 : 1'bz;  // Controlled_Buffer controlled_buffer_7
  assign CMEMBUS[10] = mxMDR2 ? 1'b1 : 1'bz;  // Controlled_Buffer controlled_buffer_8
  assign CMEMBUS[15] = decSP ? 1'b1 : 1'bz;  // Controlled_Buffer controlled_buffer_9
  assign CMEMBUS[20] = ldPC7__0 ? 1'b1 : 1'bz;  // Controlled_Buffer controlled_buffer_10
  assign CMEMBUS[21] = ldPC15__8 ? 1'b1 : 1'bz;  // Controlled_Buffer controlled_buffer_11

  // Other names for the same wires on the sheet: ldBR = inta; ADDIVTP15__0[15:0] = ADDIVTP; CLK = in_2;
  //   stFETCH = CMEMBUS[0]; mxMAR = CMEMBUS[6]; INTR_t = COMMONBUS[3]; HALT = COMMONBUS[4]; FCBUS = in_3;
  //   intrReq[7:0] = intr; PSWS = PSW[0]; PSWV = PSW[1]; PSWC = PSW[2]; PSWZ = PSW[3]; PSWN = PSW[4]; PSWI = PSW[15];
  //   rst = in_1

  // Notes on the sheet:
  //   Operaciona jedinica
  //   Upravljacka jedinica
  //   contents of rom_1 (hex, n*v repeats v):
  //   20000 1430000 47 370010 87 570010 c7 770010 107 970010 147 b70010 187 d70010 800 22 107000c 1400
  //   127000c 200 2000
endmodule

module RAM (
  input  [15:0] in_1,
  input  in_2,
  input  [7:0] in_3,
  input  in_4,
  input  in_5,
  input  in_6,
  output [7:0] DOUT,
  output out_8
);

  wire and_1_out, and_2_out, CNT0, fc, LDCNT, not_1_out, notCNT0, or_1_out, reg4_ld_sl_sr_1_p6, rsff_2_p4, sl;
  wire [3:0] CNT, LFSR;

  // RSFF rsff_1: pin names not known; wires that end beside it: 1'b0, in_2, in_6, sl
  or or_1 (or_1_out, in_4, in_5);
  // RisingEdge risingedge_1: pin names not known; wires that end beside it: or_1_out, in_2, LDCNT
  // REG4_LD_SL_SR reg4_ld_sl_sr_1: pin names not known; wires that end beside it: 1'b0, 1'b0, in_2, 4'b1111, LFSR, reg4_ld_sl_sr_1_p6, sl, in_6
  xor xor_1 (reg4_ld_sl_sr_1_p6, LFSR[2], LFSR[3]);
  and and_1 (and_1_out, CNT0, ~LDCNT);  // AND_Gate
  not not_1 (not_1_out, in_4);
  // REG4m_DEC_LD reg4m_dec_ld_1: pin names not known; wires that end beside it: in_2, LFSR, CNT, LDCNT, notCNT0, notCNT0
  or or_2 (notCNT0, CNT[0], CNT[1], CNT[2], CNT[3]);
  // RSFF rsff_2: pin names not known; wires that end beside it: and_1_out, in_2, LDCNT, rsff_2_p4
  // NOT_Gate not_2 has open pins: in=in_6, out=open
  RAM_part #(.addrWidth(16), .bus("separate")) ram_1 (
    .addr(in_1), .din(in_3), .data(DOUT), .str(in_4), .sel(1'b1), .clk(in_2), .ld(not_1_out), .clr(1'b0));
  not not_3 (CNT0, notCNT0);
  and and_2 (and_2_out, rsff_2_p4, CNT0);
  // RSFF rsff_3: pin names not known; wires that end beside it: fc, in_2, and_2_out, fc, fc, 1'b1
  // NOT_Gate not_4 has open pins: in=in_6, out=open

  assign out_8 = 1'b1;

  // Other names for the same wires on the sheet: ADR[15:0] = in_1; CLK = in_2; DIN[7:0] = in_3; RDMEM = in_5;
  //   rst = in_6; WRMEM = in_4

  // Notes on the sheet:
  //   Brojac za generisanje random broja 
  //   Random broj predstavlja vreme pristupa memoriji
  //   Jedinica za generisanje function complete (fc) signala
  //   Brojac za dekrementiranje random broja
endmodule
